# Fritzing sketch ir-arduino (saved by Fritzing 0.9.3b)
breadboards: 1

parts:
  Part1 = Arduino Uno (Rev3)
  R1 = Resistor [tolerance=±5% resistance=220 package=THT]
  R2 = Resistor [tolerance=±5% resistance=220 package=THT]
  LED1 = LED - 5mm [color="Red (633nm)" package="5 mm [THT]"]
  LED2 = LED - 5mm [color="Green (560nm)" package="5 mm [THT]"]
  SFH5110 = TSOP312.., 314.. [package=THT]

nets:
  N1: Part1.A0, R1.Pin_1
  N2: Part1.A1, R2.Pin_1
  GND: Part1.GND, LED1.cathode, LED2.cathode, SFH5110.GND
  N3: Part1.D2, SFH5110.Data
  N4: Part1.5V, SFH5110.Vs
  N5: R1.Pin_0, LED1.anode
  N6: R2.Pin_0, LED2.anode
